// Logisim project CombinedLogisim.circ as structural Verilog: 26 circuits, main circuit main
module main (
  input  Register_File,
  input  in_2
);

  wire clock_1_out, controller_1_cmpenable, controller_1_mem_read, controller_1_mem_write, controller_1_mux1,
       controller_1_mux3, controller_1_mux4, controller_1_mux5, controller_1_pc_read, controller_1_pc_write,
       controller_1_regwrite, flagfile_1_cf, flagfile_1_zf;
  wire [1:0] controller_1_mux2;
  wire [2:0] controller_1_alu_controller;
  wire [3:0] controller_1_r1, controller_1_r2, controller_1_w;
  wire [7:0] pc_1_out_2;
  wire [9:0] pc_1_out;
  wire [17:0] alu_1_result, controlled_buffer_1_out, imm6signextender_5_0_1_out_2, multiplexer_1_out,
       multiplexer_2_out, multiplexer_3_out, multiplexer_5_out, n18bitadder_1_sum, n18bitadder_2_sum,
       ram_1_data, registerfile_1_read_1_2, registerfile_1_read_2_2, rom_1_data, sign_ex_0_9_out,
       Zero_ex_0_9_out;

  Clock clock_1 (.out(clock_1_out));
  PC pc_1 (
    .Write(controller_1_pc_write), .In(multiplexer_5_out), .En(controller_1_pc_read), .Clk(clock_1_out),
    .Out({pc_1_out_2, pc_1_out}));
  _18bitAdder u_18bitadder_1 (
    .C_in(1'b0), .input_1(18'h1), .input2({pc_1_out_2, pc_1_out}), .sum(n18bitadder_1_sum));  // open: carry_out
  SignExtender10 sign_ex_0_9 (.in(rom_1_data), .out(sign_ex_0_9_out));
  zeroExtender10 Zero_ex_0_9 (.in(rom_1_data), .out(Zero_ex_0_9_out));
  ROM #(.addrWidth(10), .dataWidth(18)) rom_1 (.addr(pc_1_out), .data(rom_1_data), .sel(1'b1));
  Controller controller_1 (
    .Instruction(rom_1_data), .Clk(clock_1_out), .pc_Read(controller_1_pc_read),
    .pc_Write(controller_1_pc_write), .regWrite(controller_1_regwrite), .Mem_Write(controller_1_mem_write),
    .Mem_Read(controller_1_mem_read), .Mux2(controller_1_mux2), .Mux3(controller_1_mux3),
    .Mux4(controller_1_mux4), .Mux5(controller_1_mux5), .Alu_controller(controller_1_alu_controller),
    .Mux1(controller_1_mux1), .CmpEnable(controller_1_cmpenable), .R2(controller_1_r2), .R1(controller_1_r1),
    .W(controller_1_w), .CF(flagfile_1_cf), .ZF(flagfile_1_zf));
  FlagFile flagfile_1 (
    .Cmp_Enable(controller_1_cmpenable), .R1(registerfile_1_read_2_2), .R2(registerfile_1_read_1_2),
    .Clk(clock_1_out), .Zf(flagfile_1_zf), .Cf(flagfile_1_cf), .Clr(Register_File));
  imm6SignExtender_5_0 imm6signextender_5_0_1 (.\input (rom_1_data), .out_2(imm6signextender_5_0_1_out_2));
  _18bitAdder u_18bitadder_2 (
    .C_in(1'b0), .input_1(n18bitadder_1_sum), .input2(sign_ex_0_9_out), .sum(n18bitadder_2_sum));  // open: carry_out
  RegisterFile registerfile_1 (
    .Read_2(controller_1_r2), .Read_1(controller_1_r1), .Clr(Register_File), .Input(controlled_buffer_1_out),
    .Write_Enable(controller_1_regwrite), .Write(controller_1_w), .Clk(clock_1_out),
    .Read_1_2(registerfile_1_read_1_2), .Read_2_2(registerfile_1_read_2_2));
  Multiplexer #(.width(18), .enable("false")) multiplexer_1 (
    .in0(registerfile_1_read_2_2), .in1(imm6signextender_5_0_1_out_2), .out(multiplexer_1_out),
    .sel(controller_1_mux1));
  ALU alu_1 (
    .input1(registerfile_1_read_1_2), .input2(multiplexer_1_out), .in_2(controller_1_alu_controller),
    .result(alu_1_result));  // open: Overflow
  Multiplexer #(.select(2), .width(18), .enable("false")) multiplexer_2 (
    .in0(alu_1_result), .in1(Zero_ex_0_9_out), .in2(n18bitadder_2_sum), .in3(sign_ex_0_9_out),
    .out(multiplexer_2_out), .sel(controller_1_mux2));
  assign controlled_buffer_1_out = in_2 ? {18{1'b0}} : 18'bz;  // Controlled_Buffer controlled_buffer_1
  RAM #(.addrWidth(18), .dataWidth(18), .bus("separate")) ram_1 (
    .addr(multiplexer_2_out), .din(registerfile_1_read_2_2), .data(ram_1_data), .str(controller_1_mem_write),
    .sel(1'b1), .clk(clock_1_out), .ld(controller_1_mem_read), .clr(1'b0));
  Multiplexer #(.width(18), .enable("false")) multiplexer_3 (
    .in0(ram_1_data), .in1(multiplexer_2_out), .out(multiplexer_3_out), .sel(controller_1_mux3));
  Multiplexer #(.width(18), .enable("false")) multiplexer_4 (
    .in0(multiplexer_3_out), .in1(n18bitadder_1_sum), .out(controlled_buffer_1_out), .sel(controller_1_mux4));
  Multiplexer #(.width(18), .enable("false")) multiplexer_5 (
    .in0(multiplexer_3_out), .in1(n18bitadder_1_sum), .out(multiplexer_5_out), .sel(controller_1_mux5));

  // Notes on the sheet:
  //      PC
  //   Adder
  //   contents of rom_1 (hex, n*v repeats v):
  //   0 1040a c40 24020 0 0 5003 9403 d803 1603f 1c000 19c00 20040 20400 20000 28040 4*0 20400 2c040 4*0
  //   20040 30040 4*0 20400 34040 4*0 20000 34040
  //   TOGGLE BEFORE START!
  //   Mux1
  //   ALU
  //   Mux2
  //   Mux3
  //   Mux4
  //   Mux5
endmodule

module FlipFlop (
  input  D,
  input  Clk,
  input  Clr,
  input  Enable,
  output Q
);

  wire and_1_out, and_2_out, and_3_out, and_4_out, and_5_out, controlled_buffer_1_out, nor_1_out, nor_2_out,
       nor_4_out, not_1_out;

  and and_1 (and_1_out, ~Clk, Enable);  // AND_Gate
  and and_2 (and_2_out, D, ~and_1_out);  // AND_Gate
  and and_3 (and_3_out, ~and_1_out, ~D);  // AND_Gate
  nor nor_1 (nor_1_out, and_2_out, nor_2_out);
  nor nor_2 (nor_2_out, nor_1_out, and_3_out);
  assign controlled_buffer_1_out = not_1_out ? and_4_out : 1'bz;  // Controlled_Buffer controlled_buffer_1
  and and_4 (and_4_out, nor_1_out, and_1_out);
  and and_5 (and_5_out, and_1_out, ~nor_1_out);  // AND_Gate
  assign controlled_buffer_1_out = Clr ? 1'b1 : 1'bz;  // Controlled_Buffer controlled_buffer_2
  not not_1 (not_1_out, Clr);
  nor nor_3 (Q, controlled_buffer_1_out, nor_4_out);
  nor nor_4 (nor_4_out, Q, and_5_out);
endmodule

module Register (
  input  Clr,
  input  [17:0] D,
  input  Clk,
  input  Enable,
  output [17:0] out_5
);

  FlipFlop flipflop_1 (.D(D[16]), .Clk(Clk), .Clr(Clr), .Q(out_5[16]), .Enable(Enable));
  FlipFlop flipflop_2 (.D(D[17]), .Clk(Clk), .Clr(Clr), .Q(out_5[17]), .Enable(Enable));
  FlipFlop flipflop_3 (.D(D[15]), .Clk(Clk), .Clr(Clr), .Q(out_5[15]), .Enable(Enable));
  FlipFlop flipflop_4 (.D(D[14]), .Clk(Clk), .Clr(Clr), .Q(out_5[14]), .Enable(Enable));
  FlipFlop flipflop_5 (.D(D[13]), .Clk(Clk), .Clr(Clr), .Q(out_5[13]), .Enable(Enable));
  FlipFlop flipflop_6 (.D(D[12]), .Clk(Clk), .Clr(Clr), .Q(out_5[12]), .Enable(Enable));
  FlipFlop flipflop_7 (.D(D[11]), .Clk(Clk), .Clr(Clr), .Q(out_5[11]), .Enable(Enable));
  FlipFlop flipflop_8 (.D(D[9]), .Clk(Clk), .Clr(Clr), .Q(out_5[9]), .Enable(Enable));
  FlipFlop flipflop_9 (.D(D[10]), .Clk(Clk), .Clr(Clr), .Q(out_5[10]), .Enable(Enable));
  FlipFlop flipflop_10 (.D(D[8]), .Clk(Clk), .Clr(Clr), .Q(out_5[8]), .Enable(Enable));
  FlipFlop flipflop_11 (.D(D[7]), .Clk(Clk), .Clr(Clr), .Q(out_5[7]), .Enable(Enable));
  FlipFlop flipflop_12 (.D(D[6]), .Clk(Clk), .Clr(Clr), .Q(out_5[6]), .Enable(Enable));
  FlipFlop flipflop_13 (.D(D[5]), .Clk(Clk), .Clr(Clr), .Q(out_5[5]), .Enable(Enable));
  FlipFlop flipflop_14 (.D(D[4]), .Clk(Clk), .Clr(Clr), .Q(out_5[4]), .Enable(Enable));
  FlipFlop flipflop_15 (.D(D[3]), .Clk(Clk), .Clr(Clr), .Q(out_5[3]), .Enable(Enable));
  FlipFlop flipflop_16 (.D(D[2]), .Clk(Clk), .Clr(Clr), .Q(out_5[2]), .Enable(Enable));
  FlipFlop flipflop_17 (.D(D[1]), .Clk(Clk), .Clr(Clr), .Q(out_5[1]), .Enable(Enable));
  FlipFlop flipflop_18 (.D(D[0]), .Clk(Clk), .Clr(Clr), .Q(out_5[0]), .Enable(Enable));
endmodule

module RegisterFile (
  input  [3:0] Read_2,
  input  [3:0] Read_1,
  input  Clk,
  input  Clr,
  input  [17:0] Input,
  input  Write_Enable,
  input  [3:0] Write,
  output [17:0] Read_1_2,
  output [17:0] Read_2_2
);

  wire decoder_1_out0, decoder_1_out1, decoder_1_out2, decoder_1_out3, decoder_1_out4, decoder_1_out5,
       decoder_1_out6, decoder_1_out7, decoder_1_out8, decoder_1_out9, decoder_1_out10, decoder_1_out11,
       decoder_1_out12, decoder_1_out13, decoder_1_out14, decoder_1_out15, decoder_2_out0, decoder_2_out1,
       decoder_2_out2, decoder_2_out3, decoder_2_out4, decoder_2_out5, decoder_2_out6, decoder_2_out7,
       decoder_2_out8, decoder_2_out9, decoder_2_out10, decoder_2_out11, decoder_2_out12, decoder_2_out13,
       decoder_2_out14, decoder_2_out15, decoder_3_out0, decoder_3_out1, decoder_3_out2, decoder_3_out3,
       decoder_3_out4, decoder_3_out5, decoder_3_out6, decoder_3_out7, decoder_3_out8, decoder_3_out9,
       decoder_3_out10, decoder_3_out11, decoder_3_out12, decoder_3_out13, decoder_3_out14, decoder_3_out15;
  wire [17:0] register_1_out_5, register_2_out_5, register_3_out_5, register_4_out_5, register_5_out_5,
       register_6_out_5, register_7_out_5, register_8_out_5, register_9_out_5, register_10_out_5,
       register_11_out_5, register_12_out_5, register_13_out_5, register_14_out_5, register_15_out_5,
       register_16_out_5;

  Decoder #(.select(4), .enable("false")) decoder_1 (
    .out0(decoder_1_out0), .out1(decoder_1_out1), .out2(decoder_1_out2), .out3(decoder_1_out3),
    .out4(decoder_1_out4), .out5(decoder_1_out5), .out6(decoder_1_out6), .out7(decoder_1_out7),
    .out8(decoder_1_out8), .out9(decoder_1_out9), .out10(decoder_1_out10), .out11(decoder_1_out11),
    .out12(decoder_1_out12), .out13(decoder_1_out13), .out14(decoder_1_out14), .out15(decoder_1_out15),
    .sel(Read_2));
  Decoder #(.select(4), .enable("false")) decoder_2 (
    .out0(decoder_2_out0), .out1(decoder_2_out1), .out2(decoder_2_out2), .out3(decoder_2_out3),
    .out4(decoder_2_out4), .out5(decoder_2_out5), .out6(decoder_2_out6), .out7(decoder_2_out7),
    .out8(decoder_2_out8), .out9(decoder_2_out9), .out10(decoder_2_out10), .out11(decoder_2_out11),
    .out12(decoder_2_out12), .out13(decoder_2_out13), .out14(decoder_2_out14), .out15(decoder_2_out15),
    .sel(Read_1));
  Decoder #(.select(4), .disabled(0)) decoder_3 (
    .out0(decoder_3_out0), .out1(decoder_3_out1), .out2(decoder_3_out2), .out3(decoder_3_out3),
    .out4(decoder_3_out4), .out5(decoder_3_out5), .out6(decoder_3_out6), .out7(decoder_3_out7),
    .out8(decoder_3_out8), .out9(decoder_3_out9), .out10(decoder_3_out10), .out11(decoder_3_out11),
    .out12(decoder_3_out12), .out13(decoder_3_out13), .out14(decoder_3_out14), .out15(decoder_3_out15),
    .sel(Write), .en(Write_Enable));
  assign Read_1_2 = decoder_2_out0 ? register_1_out_5 : 18'bz;  // Controlled_Buffer controlled_buffer_1
  Register register_1 (.Clr(Clr), .Clk(Clk), .out_5(register_1_out_5), .Enable(decoder_3_out0), .D(Input));
  assign Read_2_2 = decoder_1_out0 ? register_1_out_5 : 18'bz;  // Controlled_Buffer controlled_buffer_2
  assign Read_2_2 = decoder_1_out1 ? register_2_out_5 : 18'bz;  // Controlled_Buffer controlled_buffer_3
  assign Read_1_2 = decoder_2_out1 ? register_2_out_5 : 18'bz;  // Controlled_Buffer controlled_buffer_4
  Register register_2 (.Clr(Clr), .Clk(Clk), .out_5(register_2_out_5), .Enable(decoder_3_out1), .D(Input));
  assign Read_2_2 = decoder_1_out2 ? register_3_out_5 : 18'bz;  // Controlled_Buffer controlled_buffer_5
  assign Read_1_2 = decoder_2_out2 ? register_3_out_5 : 18'bz;  // Controlled_Buffer controlled_buffer_6
  Register register_3 (.Clr(Clr), .Clk(Clk), .out_5(register_3_out_5), .Enable(decoder_3_out2), .D(Input));
  assign Read_2_2 = decoder_1_out3 ? register_4_out_5 : 18'bz;  // Controlled_Buffer controlled_buffer_7
  assign Read_1_2 = decoder_2_out3 ? register_4_out_5 : 18'bz;  // Controlled_Buffer controlled_buffer_8
  assign Read_1_2 = decoder_2_out4 ? register_5_out_5 : 18'bz;  // Controlled_Buffer controlled_buffer_9
  Register register_4 (.Clr(Clr), .Clk(Clk), .out_5(register_4_out_5), .Enable(decoder_3_out3), .D(Input));
  Register register_5 (.Clr(Clr), .Clk(Clk), .out_5(register_5_out_5), .Enable(decoder_3_out4), .D(Input));
  assign Read_2_2 = decoder_1_out5 ? register_6_out_5 : 18'bz;  // Controlled_Buffer controlled_buffer_10
  assign Read_2_2 = decoder_1_out4 ? register_5_out_5 : 18'bz;  // Controlled_Buffer controlled_buffer_11
  assign Read_1_2 = decoder_2_out5 ? register_6_out_5 : 18'bz;  // Controlled_Buffer controlled_buffer_12
  Register register_6 (.Clr(Clr), .Clk(Clk), .out_5(register_6_out_5), .Enable(decoder_3_out5), .D(Input));
  assign Read_2_2 = decoder_1_out6 ? register_7_out_5 : 18'bz;  // Controlled_Buffer controlled_buffer_13
  assign Read_1_2 = decoder_2_out6 ? register_7_out_5 : 18'bz;  // Controlled_Buffer controlled_buffer_14
  Register register_7 (.Clr(Clr), .Clk(Clk), .out_5(register_7_out_5), .Enable(decoder_3_out6), .D(Input));
  assign Read_2_2 = decoder_1_out7 ? register_9_out_5 : 18'bz;  // Controlled_Buffer controlled_buffer_15
  assign Read_1_2 = decoder_2_out8 ? register_8_out_5 : 18'bz;  // Controlled_Buffer controlled_buffer_16
  assign Read_1_2 = decoder_2_out7 ? register_9_out_5 : 18'bz;  // Controlled_Buffer controlled_buffer_17
  Register register_8 (.Clr(Clr), .Clk(Clk), .out_5(register_8_out_5), .Enable(decoder_3_out8), .D(Input));
  Register register_9 (.Clr(Clr), .Clk(Clk), .out_5(register_9_out_5), .Enable(decoder_3_out7), .D(Input));
  assign Read_2_2 = decoder_1_out8 ? register_8_out_5 : 18'bz;  // Controlled_Buffer controlled_buffer_18
  assign Read_2_2 = decoder_1_out9 ? register_10_out_5 : 18'bz;  // Controlled_Buffer controlled_buffer_19
  assign Read_1_2 = decoder_2_out9 ? register_10_out_5 : 18'bz;  // Controlled_Buffer controlled_buffer_20
  Register register_10 (.Clr(Clr), .Clk(Clk), .out_5(register_10_out_5), .Enable(decoder_3_out9), .D(Input));
  assign Read_2_2 = decoder_1_out10 ? register_11_out_5 : 18'bz;  // Controlled_Buffer controlled_buffer_21
  assign Read_1_2 = decoder_2_out10 ? register_11_out_5 : 18'bz;  // Controlled_Buffer controlled_buffer_22
  Register register_11 (.Clr(Clr), .Clk(Clk), .out_5(register_11_out_5), .Enable(decoder_3_out10), .D(Input));
  assign Read_2_2 = decoder_1_out11 ? register_13_out_5 : 18'bz;  // Controlled_Buffer controlled_buffer_23
  assign Read_1_2 = decoder_2_out12 ? register_12_out_5 : 18'bz;  // Controlled_Buffer controlled_buffer_24
  assign Read_1_2 = decoder_2_out11 ? register_13_out_5 : 18'bz;  // Controlled_Buffer controlled_buffer_25
  Register register_12 (.Clr(Clr), .Clk(Clk), .out_5(register_12_out_5), .Enable(decoder_3_out12), .D(Input));
  Register register_13 (.Clr(Clr), .Clk(Clk), .out_5(register_13_out_5), .Enable(decoder_3_out11), .D(Input));
  assign Read_2_2 = decoder_1_out13 ? register_14_out_5 : 18'bz;  // Controlled_Buffer controlled_buffer_26
  assign Read_2_2 = decoder_1_out12 ? register_12_out_5 : 18'bz;  // Controlled_Buffer controlled_buffer_27
  assign Read_1_2 = decoder_2_out13 ? register_14_out_5 : 18'bz;  // Controlled_Buffer controlled_buffer_28
  Register register_14 (.Clr(Clr), .Clk(Clk), .out_5(register_14_out_5), .Enable(decoder_3_out13), .D(Input));
  assign Read_2_2 = decoder_1_out14 ? register_15_out_5 : 18'bz;  // Controlled_Buffer controlled_buffer_29
  assign Read_1_2 = decoder_2_out14 ? register_15_out_5 : 18'bz;  // Controlled_Buffer controlled_buffer_30
  Register register_15 (.Clr(Clr), .Clk(Clk), .out_5(register_15_out_5), .Enable(decoder_3_out14), .D(Input));
  assign Read_2_2 = decoder_1_out15 ? register_16_out_5 : 18'bz;  // Controlled_Buffer controlled_buffer_31
  assign Read_1_2 = decoder_2_out15 ? register_16_out_5 : 18'bz;  // Controlled_Buffer controlled_buffer_32
  Register register_16 (.Clr(Clr), .Clk(Clk), .out_5(register_16_out_5), .Enable(decoder_3_out15), .D(Input));
endmodule

module ALU (
  input  [17:0] input1,
  input  [2:0] in_2,
  input  [17:0] input2,
  output [17:0] result,
  output Overflow
);

  wire [17:0] AND_out, n18bitadder_1_sum, not_1_out, not_2_out, OR_out;

  _18bitAdder u_18bitadder_1 (
    .C_in(1'b0), .input_1(input1), .input2(input2), .sum(n18bitadder_1_sum), .carry_out(Overflow));
  assign AND_out = input1 & input2;  // AND_Gate AND, 18 bits wide
  assign not_1_out = ~AND_out;  // NOT_Gate not_1, 18 bits wide
  assign OR_out = input1 | input2;  // OR_Gate OR, 18 bits wide
  assign not_2_out = ~OR_out;  // NOT_Gate not_2, 18 bits wide
  Multiplexer #(.select(3), .width(18)) multiplexer_1 (
    .in0(AND_out), .in1(not_1_out), .in2(OR_out), .in3(not_2_out), .in4(n18bitadder_1_sum), .out(result),
    .sel(in_2), .en(1'b1));  // open: in5, in6, in7
endmodule

module Adder (
  input  In_1,
  input  In_2,
  input  C,
  output S,
  output C_out
);

  wire and_1_out, and_2_out, xor_1_out;

  xor xor_1 (xor_1_out, In_1, In_2);
  and and_1 (and_1_out, In_1, In_2);
  and and_2 (and_2_out, xor_1_out, C);
  xor xor_2 (S, xor_1_out, C);
  or or_1 (C_out, and_2_out, and_1_out);
endmodule

module _4_bit_adder (
  input  C_in,
  input  [3:0] In_1,
  input  [3:0] In_2,
  output [3:0] Out,
  output C_out
);

  wire adder_1_c_out, adder_2_c_out, adder_3_c_out;

  Adder adder_1 (.In_1(In_1[0]), .In_2(In_2[0]), .C(C_in), .S(Out[0]), .C_out(adder_1_c_out));
  Adder adder_2 (.In_1(In_1[1]), .In_2(In_2[1]), .C(adder_1_c_out), .S(Out[1]), .C_out(adder_2_c_out));
  Adder adder_3 (.In_1(In_1[2]), .In_2(In_2[2]), .C(adder_2_c_out), .S(Out[2]), .C_out(adder_3_c_out));
  Adder adder_4 (.In_1(In_1[3]), .In_2(In_2[3]), .C(adder_3_c_out), .S(Out[3]), .C_out(C_out));
endmodule

// Add
module _6bit_Adder (
  input  C_in,
  input  [5:0] In_1,
  input  [5:0] In_2,
  output [5:0] Out,
  output C_out
);

  wire adder_1_c_out, adder_2_c_out, adder_3_c_out, adder_4_c_out, adder_5_c_out;

  Adder adder_1 (.In_1(In_1[0]), .In_2(In_2[0]), .C(C_in), .S(Out[0]), .C_out(adder_1_c_out));
  Adder adder_2 (.In_1(In_1[1]), .In_2(In_2[1]), .C(adder_1_c_out), .S(Out[1]), .C_out(adder_2_c_out));
  Adder adder_3 (.In_1(In_1[2]), .In_2(In_2[2]), .C(adder_2_c_out), .S(Out[2]), .C_out(adder_3_c_out));
  Adder adder_4 (.In_1(In_1[3]), .In_2(In_2[3]), .C(adder_3_c_out), .S(Out[3]), .C_out(adder_4_c_out));
  Adder adder_5 (.In_1(In_1[4]), .In_2(In_2[4]), .C(adder_4_c_out), .S(Out[4]), .C_out(adder_5_c_out));
  Adder adder_6 (.In_1(In_1[5]), .In_2(In_2[5]), .C(adder_5_c_out), .S(Out[5]), .C_out(C_out));
endmodule

module PC (
  input  Write,
  input  [17:0] In,
  input  En,
  input  Clk,
  output [17:0] Out
);

  wire [17:0] multiplexer_1_out;

  Multiplexer #(.width(18)) multiplexer_1 (.in0(Out), .in1(In), .out(multiplexer_1_out), .sel(Write), .en(1'b1));
  Register_part #(.width(18)) register_1 (.D(multiplexer_1_out), .en(En), .Q(Out), .clk(Clk), .clr(1'b0));
endmodule

module Sign_Extender_6 (
  input  [3:0] in_1,
  output [5:0] out_2
);


  assign out_2 = {{3{in_1[3]}}, in_1[2:0]};
endmodule

module Zero_Extender_6 (
  input  [3:0] in_1,
  output [5:0] out_2
);


  assign out_2 = {2'b00, in_1};
endmodule

module sign_Extender_12 (
  input  [5:0] in_1,
  output [17:0] out_2
);


  assign out_2 = {{13{in_1[5]}}, in_1[4:0]};
endmodule

module _8bitSignExtender (
  input  [9:0] _10_bit_input,
  output [17:0] _18_bit_output
);


  assign _18_bit_output = {{9{_10_bit_input[9]}}, _10_bit_input[8:0]};

  // Notes on the sheet:
  //   10 bit input
  //   18 bit output
endmodule

module _18bitAdder (
  input  C_in,
  input  [17:0] input_1,
  input  [17:0] input2,
  output [17:0] sum,
  output carry_out
);

  wire adder_1_c_out, adder_2_c_out, adder_3_c_out, adder_4_c_out, adder_5_c_out, adder_6_c_out,
       adder_7_c_out, adder_8_c_out, adder_9_c_out, adder_10_c_out, adder_11_c_out, adder_12_c_out,
       adder_13_c_out, adder_14_c_out, adder_15_c_out, adder_16_c_out, adder_17_c_out, adder_18_c_out;

  Adder adder_1 (.In_1(input_1[0]), .In_2(input2[0]), .C(C_in), .S(sum[0]), .C_out(adder_1_c_out));
  Adder adder_2 (.In_1(input_1[1]), .In_2(input2[1]), .C(adder_1_c_out), .S(sum[1]), .C_out(adder_2_c_out));
  Adder adder_3 (.In_1(input_1[2]), .In_2(input2[2]), .C(adder_2_c_out), .S(sum[2]), .C_out(adder_3_c_out));
  Adder adder_4 (.In_1(input_1[3]), .In_2(input2[3]), .C(adder_3_c_out), .S(sum[3]), .C_out(adder_4_c_out));
  Adder adder_5 (.In_1(input_1[4]), .In_2(input2[4]), .C(adder_4_c_out), .S(sum[4]), .C_out(adder_5_c_out));
  Adder adder_6 (.In_1(input_1[5]), .In_2(input2[5]), .C(adder_5_c_out), .S(sum[5]), .C_out(adder_6_c_out));
  Adder adder_7 (.In_1(input_1[6]), .In_2(input2[6]), .C(adder_6_c_out), .S(sum[6]), .C_out(adder_7_c_out));
  Adder adder_8 (.In_1(input_1[7]), .In_2(input2[7]), .C(adder_7_c_out), .S(sum[7]), .C_out(adder_8_c_out));
  Adder adder_9 (.In_1(input_1[8]), .In_2(input2[8]), .C(adder_8_c_out), .S(sum[8]), .C_out(adder_9_c_out));
  Adder adder_10 (.In_1(input_1[9]), .In_2(input2[9]), .C(adder_9_c_out), .S(sum[9]), .C_out(adder_10_c_out));
  Adder adder_11 (.In_1(input_1[10]), .In_2(input2[10]), .C(adder_10_c_out), .S(sum[10]), .C_out(adder_11_c_out));
  Adder adder_12 (.In_1(input_1[11]), .In_2(input2[11]), .C(adder_11_c_out), .S(sum[11]), .C_out(adder_12_c_out));
  Adder adder_13 (.In_1(input_1[12]), .In_2(input2[12]), .C(adder_12_c_out), .S(sum[12]), .C_out(adder_13_c_out));
  Adder adder_14 (.In_1(input_1[13]), .In_2(input2[13]), .C(adder_13_c_out), .S(sum[13]), .C_out(adder_14_c_out));
  Adder adder_15 (.In_1(input_1[14]), .In_2(input2[14]), .C(adder_14_c_out), .S(sum[14]), .C_out(adder_15_c_out));
  Adder adder_16 (.In_1(input_1[15]), .In_2(input2[15]), .C(adder_15_c_out), .S(sum[15]), .C_out(adder_16_c_out));
  Adder adder_17 (.In_1(input_1[16]), .In_2(input2[16]), .C(adder_16_c_out), .S(sum[16]), .C_out(adder_17_c_out));
  Adder adder_18 (.In_1(input_1[17]), .In_2(input2[17]), .C(adder_17_c_out), .S(sum[17]), .C_out(adder_18_c_out));

  // Notes on the sheet:
  //   Input 1
  //   Input 2
  //   Carry out
endmodule

module imm6SignExtender_5_0 (
  input  [17:0] \input ,
  output [17:0] out_2
);


  assign out_2 = {{13{\input [5]}}, \input [4:0]};
endmodule

module adressInstr_9_0 (
  input  [17:0] \input ,
  output [17:0] adressPart
);


  assign adressPart = {{9{\input [9]}}, \input [8:0]};
endmodule

module addressInstr_13_4 (
  input  [17:0] \input ,
  output [17:0] out_2
);


  assign out_2 = {{9{\input [13]}}, \input [12:4]};
endmodule

module Comparator (
  input  [17:0] R1,
  input  [17:0] R2,
  output R1bigger,
  output R2bigger,
  output eq
);

  wire and_1_out, and_3_out, and_4_out, not_1_out, or_1_out, or_2_out, or_3_out, subtractor18_1_underflow,
       xor_1_out, xor_2_out, xor_3_out, xor_4_out, xor_5_out;
  wire [17:0] xnor_1_out;

  assign xnor_1_out = ~(R2 ^ R1);  // XNOR_Gate xnor_1, 18 bits wide
  and and_1 (and_1_out, R1[17], R2[17]);
  Subtractor18 subtractor18_1 (.R1(R1), .R2(R2), .Underflow(subtractor18_1_underflow));  // open: out_3, Negative_check
  xor xor_1 (xor_1_out, and_1_out, R1[17]);
  xor xor_2 (xor_2_out, and_1_out, R2[17]);
  and and_2 (eq, xnor_1_out[0], xnor_1_out[1], xnor_1_out[2], xnor_1_out[3], xnor_1_out[4], xnor_1_out[5], xnor_1_out[6], xnor_1_out[7], xnor_1_out[8], xnor_1_out[9], xnor_1_out[10], xnor_1_out[11], xnor_1_out[12], xnor_1_out[13], xnor_1_out[14], xnor_1_out[15], xnor_1_out[16], xnor_1_out[17]);
  not not_1 (not_1_out, subtractor18_1_underflow);
  xor xor_3 (xor_3_out, not_1_out, eq);
  xor xor_4 (xor_4_out, subtractor18_1_underflow, xor_2_out);
  xor xor_5 (xor_5_out, xor_1_out, xor_3_out);
  or or_1 (or_1_out, xor_1_out, xor_4_out);
  and and_3 (and_3_out, and_1_out, or_2_out);
  and and_4 (and_4_out, or_1_out, and_1_out);
  or or_2 (or_2_out, xor_2_out, xor_5_out);
  or or_3 (or_3_out, and_3_out, and_4_out);
  xor xor_6 (R1bigger, or_2_out, or_3_out);
  xor xor_7 (R2bigger, or_3_out, or_1_out);
endmodule

module Subtractor2 (
  input  R1,
  input  R2,
  input  Bin,
  output Out,
  output Borrow
);

  wire halfsubtractor_1_borrow, halfsubtractor_1_out, halfsubtractor_2_borrow;

  HalfSubtractor halfsubtractor_1 (.R1(R1), .R2(R2), .Out(halfsubtractor_1_out), .Borrow(halfsubtractor_1_borrow));
  HalfSubtractor halfsubtractor_2 (.R1(halfsubtractor_1_out), .R2(Bin), .Out(Out), .Borrow(halfsubtractor_2_borrow));
  or or_1 (Borrow, halfsubtractor_2_borrow, halfsubtractor_1_borrow);
endmodule

module HalfSubtractor (
  input  R1,
  input  R2,
  output Out,
  output Borrow
);

  wire not_1_out;

  not not_1 (not_1_out, R1);
  xor xor_1 (Out, R1, R2);
  and and_1 (Borrow, R2, not_1_out);
endmodule

module Subtractor18 (
  input  [17:0] R1,
  input  [17:0] R2,
  output [17:0] out_3,
  output Negative_check,
  output Underflow
);

  wire subtractor2_1_borrow, subtractor2_2_borrow, subtractor2_3_borrow, subtractor2_4_borrow,
       subtractor2_5_borrow, subtractor2_6_borrow, subtractor2_7_borrow, subtractor2_8_borrow,
       subtractor2_9_borrow, subtractor2_10_borrow, subtractor2_11_borrow, subtractor2_12_borrow,
       subtractor2_13_borrow, subtractor2_14_borrow, subtractor2_15_borrow, subtractor2_16_borrow,
       subtractor2_17_borrow;

  Subtractor2 subtractor2_1 (.R1(R1[0]), .R2(R2[0]), .Bin(1'b0), .Out(out_3[0]), .Borrow(subtractor2_1_borrow));
  Subtractor2 subtractor2_2 (
    .R1(R1[1]), .R2(R2[1]), .Bin(subtractor2_1_borrow), .Out(out_3[1]), .Borrow(subtractor2_2_borrow));
  Subtractor2 subtractor2_3 (
    .R1(R1[3]), .R2(R2[3]), .Bin(subtractor2_4_borrow), .Out(out_3[3]), .Borrow(subtractor2_3_borrow));
  Subtractor2 subtractor2_4 (
    .R1(R1[2]), .R2(R2[2]), .Bin(subtractor2_2_borrow), .Out(out_3[2]), .Borrow(subtractor2_4_borrow));
  Subtractor2 subtractor2_5 (
    .R1(R1[4]), .R2(R2[4]), .Bin(subtractor2_3_borrow), .Out(out_3[4]), .Borrow(subtractor2_5_borrow));
  Subtractor2 subtractor2_6 (
    .R1(R1[5]), .R2(R2[5]), .Bin(subtractor2_5_borrow), .Out(out_3[5]), .Borrow(subtractor2_6_borrow));
  Subtractor2 subtractor2_7 (
    .R1(R1[6]), .R2(R2[6]), .Bin(subtractor2_6_borrow), .Out(out_3[6]), .Borrow(subtractor2_7_borrow));
  Subtractor2 subtractor2_8 (
    .R1(R1[7]), .R2(R2[7]), .Bin(subtractor2_7_borrow), .Out(out_3[7]), .Borrow(subtractor2_8_borrow));
  Subtractor2 subtractor2_9 (
    .R1(R1[8]), .R2(R2[8]), .Bin(subtractor2_8_borrow), .Out(out_3[8]), .Borrow(subtractor2_9_borrow));
  Subtractor2 subtractor2_10 (
    .R1(R1[9]), .R2(R2[9]), .Bin(subtractor2_9_borrow), .Out(out_3[9]), .Borrow(subtractor2_10_borrow));
  Subtractor2 subtractor2_11 (
    .R1(R1[10]), .R2(R2[10]), .Bin(subtractor2_10_borrow), .Out(out_3[10]), .Borrow(subtractor2_11_borrow));
  Subtractor2 subtractor2_12 (
    .R1(R1[11]), .R2(R2[11]), .Bin(subtractor2_11_borrow), .Out(out_3[11]), .Borrow(subtractor2_12_borrow));
  Subtractor2 subtractor2_13 (
    .R1(R1[12]), .R2(R2[12]), .Bin(subtractor2_12_borrow), .Out(out_3[12]), .Borrow(subtractor2_13_borrow));
  Subtractor2 subtractor2_14 (
    .R1(R1[13]), .R2(R2[13]), .Bin(subtractor2_13_borrow), .Out(out_3[13]), .Borrow(subtractor2_14_borrow));
  Subtractor2 subtractor2_15 (
    .R1(R1[14]), .R2(R2[14]), .Bin(subtractor2_14_borrow), .Out(out_3[14]), .Borrow(subtractor2_15_borrow));
  Subtractor2 subtractor2_16 (
    .R1(R1[15]), .R2(R2[15]), .Bin(subtractor2_15_borrow), .Out(out_3[15]), .Borrow(subtractor2_16_borrow));
  Subtractor2 subtractor2_17 (
    .R1(R1[16]), .R2(R2[16]), .Bin(subtractor2_16_borrow), .Out(out_3[16]), .Borrow(subtractor2_17_borrow));
  Subtractor2 subtractor2_18 (
    .R1(R1[17]), .R2(R2[17]), .Bin(subtractor2_17_borrow), .Out(Negative_check), .Borrow(Underflow));

  assign out_3[17] = Negative_check;
endmodule

module Controller (
  input  [17:0] Instruction,
  input  CF,
  input  ZF,
  input  Clk,
  output pc_Read,
  output pc_Write,
  output Mux5,
  output [1:0] Mux2,
  output Mux1,
  output [3:0] R2,
  output [3:0] R1,
  output Mux3,
  output [3:0] W,
  output Mux4,
  output [2:0] Alu_controller,
  output Mem_Read,
  output Mem_Write,
  output regWrite,
  output CmpEnable
);

  wire and_1_out, and_2_out, and_3_out, and_4_out, and_5_out, and_6_out, and_7_out, and_8_out,
       decoder_1_out0, decoder_1_out1, decoder_1_out4, decoder_1_out5, decoder_1_out6, decoder_1_out7,
       decoder_1_out8, decoder_1_out9, decoder_1_out10, decoder_1_out12, decoder_1_out15, decoder_1_out16,
       decoder_1_out17, decoder_1_out18, decoder_1_out19, decoder_1_out20, nor_1_out, not_1_out, or_1_out,
       or_2_out, or_4_out, or_9_out, or_11_out, register_2_q;
  wire [1:0] or_6_out;
  wire [4:0] controlled_buffer_3_out, opdecider_1_out_5, register_1_q;

  OpDecider opdecider_1 (
    ._0(Instruction[14]), ._1(Instruction[15]), ._2(Instruction[16]), ._3(Instruction[17]),
    .out_5(opdecider_1_out_5));
  and and_1 (and_1_out, Instruction[17], ~Instruction[16], ~Instruction[15], ~Instruction[14]);  // AND_Gate
  not not_1 (not_1_out, and_1_out);
  assign R2 = not_1_out ? Instruction[3:0] : 4'bz;  // Controlled_Buffer controlled_buffer_1
  assign R2 = and_1_out ? Instruction[13:10] : 4'bz;  // Controlled_Buffer controlled_buffer_2
  assign controlled_buffer_3_out = decoder_1_out12 ? 5'b01101 : 5'bz;  // Controlled_Buffer controlled_buffer_3
  Register_part #(.width(5)) register_1 (
    .D(controlled_buffer_3_out), .en(1'b1), .Q(register_1_q), .clk(Clk), .clr(register_2_q));
  assign controlled_buffer_3_out = decoder_1_out0 ? 5'b00001 : 5'bz;  // Controlled_Buffer controlled_buffer_4
  assign controlled_buffer_3_out = and_3_out ? opdecider_1_out_5 : 5'bz;  // Controlled_Buffer controlled_buffer_5
  Register_part #(.width(1)) register_2 (.D(and_2_out), .en(1'b1), .Q(register_2_q), .clk(Clk));  // open: clr
  and and_2 (and_2_out, ~decoder_1_out1, ~decoder_1_out0);  // AND_Gate
  and and_3 (and_3_out, ~decoder_1_out0, ~decoder_1_out12);  // AND_Gate
  or or_1 (or_1_out, CF, ZF);
  and and_4 (and_4_out, or_1_out, decoder_1_out20);
  and and_5 (and_5_out, ~CF, decoder_1_out19);  // AND_Gate
  Decoder #(.select(5), .enable("false")) decoder_1 (
    .out0(decoder_1_out0), .out1(decoder_1_out1), .out4(decoder_1_out4), .out5(decoder_1_out5),
    .out6(decoder_1_out6), .out7(decoder_1_out7), .out8(decoder_1_out8), .out9(decoder_1_out9),
    .out10(decoder_1_out10), .out11(CmpEnable), .out12(decoder_1_out12), .out14(Mem_Write),
    .out15(decoder_1_out15), .out16(decoder_1_out16), .out17(decoder_1_out17), .out18(decoder_1_out18),
    .out19(decoder_1_out19), .out20(decoder_1_out20), .sel(register_1_q));  // open: out2, out3, out13, out21, out22, out23, out24, out25, out26, out27, out28, out29, out30, out31
  and and_6 (and_6_out, ~CF, ~ZF, decoder_1_out17);  // AND_Gate
  and and_7 (and_7_out, CF, ~ZF, decoder_1_out18);  // AND_Gate
  and and_8 (and_8_out, ZF, ~CF, decoder_1_out16);  // AND_Gate
  or or_2 (or_2_out, decoder_1_out9, Mem_Write, decoder_1_out12, decoder_1_out12, decoder_1_out10, decoder_1_out8, decoder_1_out7, decoder_1_out6, decoder_1_out5, decoder_1_out4);
  or or_3 (pc_Write, or_2_out, decoder_1_out15, and_8_out, and_6_out, decoder_1_out12, and_4_out, and_5_out, and_7_out, CmpEnable);
  not not_2 (Mux5, or_4_out);
  or or_4 (or_4_out, decoder_1_out15, decoder_1_out20, decoder_1_out19, decoder_1_out18, decoder_1_out17, decoder_1_out16);
  or or_5 (or_6_out[1], decoder_1_out15, decoder_1_out16, decoder_1_out17, decoder_1_out18, decoder_1_out19, decoder_1_out20);
  or or_6 (or_6_out[0], Mem_Write, decoder_1_out12, decoder_1_out12);
  or or_7 (Mux1, decoder_1_out9, decoder_1_out10);
  or or_8 (Mux3, decoder_1_out4, decoder_1_out5, decoder_1_out6, decoder_1_out7, decoder_1_out8, decoder_1_out9, decoder_1_out10, decoder_1_out15, decoder_1_out16, decoder_1_out17, decoder_1_out18, decoder_1_out19, decoder_1_out20);
  or or_9 (or_9_out, decoder_1_out4, decoder_1_out9);
  not not_3 (Mem_Read, Mem_Write);
  or or_10 (regWrite, decoder_1_out10, decoder_1_out9, decoder_1_out8, decoder_1_out7, decoder_1_out6, decoder_1_out5, decoder_1_out4, decoder_1_out12);
  Multiplexer #(.select(2), .width(2), .enable("false")) multiplexer_1 (
    .in0(2'b00), .in1(2'b01), .in2(2'b10), .in3(2'b11), .out(Mux2), .sel(or_6_out));
  or or_11 (or_11_out, decoder_1_out10, decoder_1_out5);
  assign Alu_controller = decoder_1_out6 ? 3'b001 : 3'bz;  // Controlled_Buffer controlled_buffer_6
  assign Alu_controller = decoder_1_out7 ? 3'b010 : 3'bz;  // Controlled_Buffer controlled_buffer_7
  assign Alu_controller = or_11_out ? 3'b000 : 3'bz;  // Controlled_Buffer controlled_buffer_8
  nor nor_1 (nor_1_out, decoder_1_out6, decoder_1_out8, decoder_1_out7, decoder_1_out5, or_9_out);
  assign Alu_controller = or_9_out ? 3'b100 : 3'bz;  // Controlled_Buffer controlled_buffer_9
  assign Alu_controller = decoder_1_out8 ? 3'b011 : 3'bz;  // Controlled_Buffer controlled_buffer_10
  assign Alu_controller = nor_1_out ? 3'b000 : 3'bz;  // Controlled_Buffer controlled_buffer_11

  assign Mux4 = 1'b0;
  assign pc_Read = 1'b1;
  assign R1 = Instruction[9:6];
  assign W = Instruction[13:10];

  // Notes on the sheet:
  //   New State
  //   ld2
  //   state to take from opcode
  //   Current State
  //   reset state
  //   if not fetch
  //   ld check
  //   check if instruction fetch state
  //   Conditional Jumps
  //   Decoder for states
  //   Pc Read
  //   Ins Read
  //   ADD
  //   AND
  //   NAND
  //   OR
  //   NOR
  //   ADDI
  //   ANDI
  //   Comp
  //   Load
  //   Load2
  //   Store
  //   Jump
  //   Ja
  //   Jb
  //   Jae
  //   Jbe
  //   001
  //   100
  //   011
  //   010
  //   001
  //   000
  //   100
  //   010
  //   001
endmodule

module SignExtender10 (
  input  [17:0] in,
  output [17:0] out
);


  assign out = {{9{in[13]}}, in[12:4]};
endmodule

module zeroExtender10 (
  input  [17:0] in,
  output [17:0] out
);


  assign out = {{8{1'b0}}, in[9:0]};
endmodule

module FlagFile (
  input  Clr,
  input  Cmp_Enable,
  input  [17:0] R1,
  input  [17:0] R2,
  input  Clk,
  output Zf,
  output Cf
);

  wire comparator_1_eq, comparator_1_r1bigger, comparator_1_r2bigger;
  wire [17:0] and_2_out;
  wire [17:2] register_1_out_5;

  Register register_1 (.Clr(Clr), .Clk(Clk), .out_5({register_1_out_5, Cf, Zf}), .Enable(Cmp_Enable), .D(and_2_out));
  Comparator comparator_1 (
    .R1(R1), .R2(R2), .R1bigger(comparator_1_r1bigger), .R2bigger(comparator_1_r2bigger), .eq(comparator_1_eq));
  and and_1 (and_2_out[1], ~comparator_1_r1bigger, ~comparator_1_eq, comparator_1_r2bigger);  // AND_Gate
  and and_2 (and_2_out[0], ~comparator_1_r1bigger, ~comparator_1_r2bigger, comparator_1_eq);  // AND_Gate

  // Notes on the sheet:
  //   Cf
  //   Zf
endmodule

module OpDecider (
  input  _0,
  input  _1,
  input  _2,
  input  _3,
  output [4:0] out_5
);

  wire and_1_out, and_2_out, and_3_out, and_4_out, and_5_out, and_6_out, and_7_out, and_8_out, and_9_out,
       and_10_out, and_11_out, and_12_out, and_13_out, and_14_out, and_15_out;

  and and_1 (and_1_out, ~_0, ~_1, ~_2, ~_3);  // AND_Gate
  and and_2 (and_2_out, _0, ~_1, ~_2, ~_3);  // AND_Gate
  and and_3 (and_3_out, ~_0, _1, ~_2, ~_3);  // AND_Gate
  and and_4 (and_4_out, _0, _1, ~_2, ~_3);  // AND_Gate
  and and_5 (and_5_out, ~_0, ~_1, _2, ~_3);  // AND_Gate
  and and_6 (and_6_out, _0, ~_1, _2, ~_3);  // AND_Gate
  and and_7 (and_7_out, ~_0, _1, _2, ~_3);  // AND_Gate
  and and_8 (and_8_out, _0, _1, _2, ~_3);  // AND_Gate
  and and_9 (and_9_out, ~_0, ~_1, ~_2, _3);  // AND_Gate
  and and_10 (and_10_out, _0, ~_1, ~_2, _3);  // AND_Gate
  and and_11 (and_11_out, ~_0, _1, ~_2, _3);  // AND_Gate
  and and_12 (and_12_out, _0, _1, ~_2, _3);  // AND_Gate
  and and_13 (and_13_out, ~_0, ~_1, _2, _3);  // AND_Gate
  and and_14 (and_14_out, _0, ~_1, _2, _3);  // AND_Gate
  and and_15 (and_15_out, ~_0, _1, _2, _3);  // AND_Gate
  assign out_5 = and_1_out ? 5'b00100 : 5'bz;  // Controlled_Buffer controlled_buffer_1
  assign out_5 = and_2_out ? 5'b00101 : 5'bz;  // Controlled_Buffer controlled_buffer_2
  assign out_5 = and_3_out ? 5'b00110 : 5'bz;  // Controlled_Buffer controlled_buffer_3
  assign out_5 = and_4_out ? 5'b01000 : 5'bz;  // Controlled_Buffer controlled_buffer_4
  assign out_5 = and_5_out ? 5'b01001 : 5'bz;  // Controlled_Buffer controlled_buffer_5
  assign out_5 = and_6_out ? 5'b01010 : 5'bz;  // Controlled_Buffer controlled_buffer_6
  assign out_5 = and_7_out ? 5'b01100 : 5'bz;  // Controlled_Buffer controlled_buffer_7
  assign out_5 = and_8_out ? 5'b01110 : 5'bz;  // Controlled_Buffer controlled_buffer_8
  assign out_5 = and_9_out ? 5'b01011 : 5'bz;  // Controlled_Buffer controlled_buffer_9
  assign out_5 = and_10_out ? 5'b01111 : 5'bz;  // Controlled_Buffer controlled_buffer_10
  assign out_5 = and_11_out ? 5'b10000 : 5'bz;  // Controlled_Buffer controlled_buffer_11
  assign out_5 = and_12_out ? 5'b10001 : 5'bz;  // Controlled_Buffer controlled_buffer_12
  assign out_5 = and_13_out ? 5'b10010 : 5'bz;  // Controlled_Buffer controlled_buffer_13
  assign out_5 = and_14_out ? 5'b10011 : 5'bz;  // Controlled_Buffer controlled_buffer_14
  assign out_5 = and_15_out ? 5'b10100 : 5'bz;  // Controlled_Buffer controlled_buffer_15

  // Notes on the sheet:
  //   00100
  //   00101
  //   00110
  //   01000
  //   01001
  //   01010
  //   01100
  //   01110
  //   01011
  //   01111
  //   10000
  //   10001
  //   10010
  //   10011
  //   10100
endmodule
